// Logisim project Sim8.circ as structural Verilog
module Addresser (
  input  [7:0] Data,
  input  [7:0] Bank_Address,
  output [15:0] Address
);

  Counter PC (.D(Data));  // open: load, count, Q, carry, clk, clr
  Register IB (.D(Data));  // open: en, Q, clk, clr
  Register D1 (.D(Data));  // open: en, Q, clk, clr
  Register D2 (.D(Data));  // open: en, Q, clk, clr
endmodule
